# Fritzing sketch CircuitDiagram (saved by Fritzing 0.9.3b)
breadboards: 1

parts:
  Part1 = Arduino Uno (Rev3) - ICSP
  S1 = Momentary Switch [package=ksa_sealed_tac_switch]  # not connected
  LED1 = smd LED [color="Green (570nm)" package="0603 [SMD]"]  # not connected
  LED2 = smd LED [color="Red (633nm)" package="0603 [SMD]"]
  R1 = Resistor [tolerance=±5% resistance=220 package="2512 [SMD]"]  # not connected
  R2 = Resistor [tolerance=±5% resistance=10k package="2512 [SMD]"]  # not connected
  LED3 = smd LED [color="Green (570nm)" package="1206 [SMD]"]
  LED3_2 = smd LED [color="Green (570nm)" package="1206 [SMD]"]
  R3 = Resistor [tolerance=±5% resistance=220 package="2512 [SMD]"]
  LED4 = smd LED [color="Green (570nm)" package="1206 [SMD]"]
  R4 = Resistor [tolerance=±5% resistance=220 package="2512 [SMD]"]
  LED5 = smd LED [color="Green (570nm)" package="1206 [SMD]"]
  LED6 = smd LED [color="Green (570nm)" package="1206 [SMD]"]
  R5 = Resistor [tolerance=±5% resistance=220 package="2512 [SMD]"]
  R6 = Resistor [tolerance=±5% resistance=220 package="2512 [SMD]"]
  S2 = Momentary Switch [package=ksa_sealed_tac_switch]
  S3 = Momentary Switch [package=ksa_sealed_tac_switch]
  S4 = Momentary Switch [package=ksa_sealed_tac_switch]
  S5 = Momentary Switch [package=ksa_sealed_tac_switch]
  R7 = Resistor [tolerance=±5% resistance=10k package="2512 [SMD]"]
  R8 = Resistor [tolerance=±5% resistance=10k package="2512 [SMD]"]
  R9 = Resistor [tolerance=±5% resistance=10k package="2512 [SMD]"]
  R10 = Resistor [tolerance=±5% resistance=10k package="2512 [SMD]"]
  R11 = Resistor [tolerance=±5% resistance=220 package="2512 [SMD]"]
  R12 = Rotary Potentiometer (Small) [maximum_resistance=100kΩ package=THT]  # not connected
  R13 = Rotary Potentiometer (Small) [maximum_resistance=100kΩ package=THT]

nets:
  N1: Part1.A0, R13.wiper
  N2: Part1.D8, S4.3
  N3: Part1.D9_PWM, S5.3
  N4: Part1.D11_PWM/MOSI, LED2.anode
  N5: Part1.D2, LED3.anode, LED3_2.anode
  N6: Part1.D3_PWM, LED4.anode
  N7: Part1.D4, LED5.anode
  N8: Part1.D5_PWM, LED6.anode
  N9: Part1.D6_PWM, S2.3
  N10: Part1.D7, S3.3
  N11: Part1.5V, S2.1, S3.1, S4.1, S5.1, R13.leg2
  N12: Part1.GND, R3.Pin_1, R4.Pin_1, R5.Pin_1, R6.Pin_1, R7.Pin_1, R8.Pin_1, R9.Pin_1, R10.Pin_1, R11.Pin_1, R13.leg1
  N13: LED2.cathode, R11.Pin_0
  N14: LED3.cathode, LED3_2.cathode, R3.Pin_0
  N15: LED4.cathode, R4.Pin_0
  N16: LED5.cathode, R5.Pin_0
  N17: LED6.cathode, R6.Pin_0
  N18: S2.4, R7.Pin_0
  N19: S3.4, R9.Pin_0
  N20: S4.4, R8.Pin_0
  N21: S5.4, R10.Pin_0
